# Fritzing sketch tv remote control  (saved by Fritzing 0.9.6b)
circuit board: 8.46667cm x 5.64444cm

parts:
  R1 = Resistor [tolerance=±5% power=0.25 resistance=10k package=THT]
  R2 = Resistor [tolerance=±5% power=0.25 resistance=1k package=THT]
  C1 = Ceramic Capacitor [capacitance=10nF voltage=35V package="100 mil [THT, multilayer]"]
  R3 = Resistor [tolerance=±5% power=0.25 resistance=470 package=THT]
  U1 = 555 Timer [package="DIP8 [THT]"]
  D2 = Diode [package=diode-1n4148]
  D3 = LTE-302 [package=lte-302]
  Q1 = TRANSISTOR_NPN [package=to-92]
  R4 = Resistor [tolerance=±5% power=0.25 resistance=1k package=THT]
  VCC1 = Battery block 9V
  D1 = Diode [package=diode-1n4148]

nets:
  N1: R1.Pin_0, R2.Pin_0
  N2: R1.Pin_1, R3.Pin_1, U1.Output
  N3: R2.Pin_1, C1.1, U1.Trigger, U1.Threshold
  N4: C1.0, U1.Ground, U1.Control_Voltage, D2.C, R4.Pin_1
  N5: R3.Pin_0, Q1.B, D1.A
  N6: U1.Vcc_Supply_Voltage, VCC1.+
  N7: D2.A, D1.C
  N8: D3.A, VCC1.-
  N9: D3.C, Q1.C
  N10: Q1.E, R4.Pin_0
